# Fritzing sketch vONE (saved by Fritzing 0.9.3b)
circuit board: 8.15cm x 4.72cm

parts:
  U1 = atmega168 [package=dip]
  J1 = female pin header, 14 pins [form="♀ (female)"]
  J2 = female pin header, 14 pins [form="♀ (female)"]
  R1 = Resistor [tolerance=±5% resistance=1k package=THT]
  U2 = Voltage Regulator - 5V [package="TO220 [THT]"]
  C1 = Electrolytic Capacitor [capacitance=1µF package="100 mil [THT, electrolytic]"]
  D1 = Rectifier Diode [part_number=1N4001 package="300 mil [THT]"]
  C2 = Electrolytic Capacitor [capacitance=1µF package="100 mil [THT, electrolytic]"]
  Power_plug1 = Power plug
  S1 = Pushbutton [package="[THT]"]
  J3 = female pin header, 6 pins [form="♀ (female)"]
  XTAL1 = Crystal [frequency="16 Mhz" package=THT]
  C3 = Ceramic Capacitor [capacitance=100nF package="200 mil [THT, multilayer]"]
  C5 = Ceramic Capacitor [capacitance=22pF package="200 mil [THT, multilayer]"]
  C4 = Ceramic Capacitor [capacitance=22pF package="200 mil [THT, multilayer]"]
  R3 = Resistor [tolerance=±5% resistance=220 package=THT]
  LED = LED - 5mm [color="Red (633nm)" package="5 mm [THT]"]
  J4 = female pin header, 5 pins [form="♀ (female)"]
  J5 = female pin header, 5 pins [form="♀ (female)"]
  J6 = female pin header, 5 pins [form="♀ (female)"]
  U5 = Voltage Regulator - 3.3V [package="TO220 [THT]"]

nets:
  N1: U1.RESET, J2.pin14, R1.Pin_0, S1.Pin_1, S1.Pin_2, C3.1
  N2: U1.D0_(RX), J2.pin13, J3.pin4
  N3: U1.D1_(TX), J2.pin12, J3.pin5
  N4: U1.D2, J2.pin11
  N5: U1.D3_(PWM), J2.pin10
  N6: U1.D4, J2.pin9
  N7: U1.VCC, U1.AVCC, U1.AREF, J1.pin8, J1.pin9, J2.pin8, R1.Pin_1, U2.output_voltage, C1.+, J3.pin3, J5.pin1, J5.pin2, J5.pin3, J5.pin4, J5.pin5, U5.input_voltage
  GND: U1.GND, J1.pin7, J2.pin7, U2.GND, C1.-, C2.-, Power_plug1.GND, S1.Pin_3, S1.Pin_4, C5.1, C4.1, LED.cathode, J4.pin1, J4.pin2, J4.pin3, J4.pin4, J4.pin5, U5.GND
  N8: U1.XLAT1, J2.pin6, XTAL1.pin_0, C5.0
  N9: U1.XLAT2, J2.pin5, XTAL1.pin_1, C4.0
  N10: U1.D5_(PWM), J2.pin4
  N11: U1.D6_(PWM), J2.pin3
  N12: U1.D7, J2.pin2
  N13: U1.D8, J2.pin1
  N14: U1.D9_(PWM), J1.pin14
  N15: U1.D10_(PWM), J1.pin13
  N16: U1.D11_(PWM), J1.pin12
  N17: U1.D12, J1.pin11
  N18: U1.D13, J1.pin10
  N19: U1.A0, J1.pin6
  N20: U1.A1, J1.pin5
  N21: U1.A2, J1.pin4
  N22: U1.A3, J1.pin3
  N23: U1.A4, J1.pin2
  N24: U1.A5, J1.pin1
  N25: U2.input_voltage, D1.cathode, C2.+
  N26: D1.anode, Power_plug1.VCC, R3.Pin_1
  N27: J3.pin6, C3.0
  N28: R3.Pin_0, LED.anode
  N29: J6.pin1, J6.pin2, J6.pin3, J6.pin4, J6.pin5, U5.output_voltage

notes:
  Atmega - 328
  16-MHZ
  22-PF
  1K
  TO220
  100-NF
  9V
  IN4001
  6.3V 1UF
  -
  +
  A5 A4 A3 A2 A1 A0
  GND
  AREF
  VCC
  13 12 11 10 9
  RESET
  RX TX D2 D3 D4
  ~
  CR CR D5 D6 D7 D8
  DTR
  TX RX
  220
  CTS
  FTDI
  Analog
  5v
  Gnd
  3.3V
  www.sashwat.in
  vONE
  ver 3.0
  LM1117

// code stored in the sketch: vONE.ino

